# Fritzing sketch PC Light Controller (saved by Fritzing 0.9.4)
circuit board: 11cm x 6cm
breadboards: 1

parts:
  NodeMCU = NodeMCU V3.0
  LM2596 = RioRand LM2596
  LLC = I2C level shifter bidirectional
  INPUT = Screw terminal - 2 pins [package=THT]
  OUTPUT = Camdenboss CTB0158-3 [part_number=CTB0158-3 package=THT]

nets:
  N1: NodeMCU.D4, LLC.LV4
  N2: NodeMCU.3V3, LLC.LV
  N3: NodeMCU.GND#6, NodeMCU.GND#13, NodeMCU.GND#16, NodeMCU.GND#33, LM2596.Pin_4, LLC.GND, OUTPUT.pin1
  N4: NodeMCU.Vin, LM2596.Pin_3, LLC.HV, OUTPUT.pin3
  N5: LM2596.Pin_1, INPUT.pin2
  N6: LM2596.Pin_2, INPUT.pin1
  N7: LLC.HV4, OUTPUT.pin2

notes:
  WS2811B Controller
  rev. 1.0 - © Rudy de Lorenzo
  GND
  V
  in
  5V
  out
  D

custom parts:
  NodeMCU V3.0: ESP8266 based NodeMCU
